// Logisim project mux.circ as structural Verilog: 1 circuit, main circuit main
module main (
  input  SW_9,
  input  SW_0,
  input  SW_1,
  output LEDR_0
);

  wire n7404_1_p2, n7408_1_p3, n7408_1_p6;

  // _7404 7404_1: pin names not known; wires that end beside it: SW_9, n7404_1_p2
  // _7408 7408_1: pin names not known; wires that end beside it: SW_0, n7404_1_p2, n7408_1_p3, SW_9, SW_1, n7408_1_p6
  // _7432 7432_1: pin names not known; wires that end beside it: n7408_1_p3, n7408_1_p6, LEDR_0

  // Notes on the sheet:
  //   mux 2:1 implemented using 7400 series
  //   v7404
  //   1
  //   2
  //   w1
  //   4
  //   5
  //   6
  //   w2
  //   v7408
  //   1
  //   2
  //   3
  //   w3
  //   v7432
  //   1
  //   2
  //   3
endmodule
